# Fritzing sketch arduino_final (saved by Fritzing 0.9.3b)
breadboards: 1

parts:
  Part1 = Arduino Uno (Rev3) - ICSP
  Part2 = RFID-RC522-v2
  kEYPAD_MATRICIAL_1 = KEYPAD 4x3
  M1 = DC Motor
  M2 = DC Motor
  M3 = DC Motor
  L298N1 = L298N DC motor driver
  Part3 = Thermal Printer
  VCC1 = Battery block 9V

nets:
  N1: Part1.A0, Part3.TXD
  N2: Part1.A1, Part3.RXD
  N3: Part1.A2, kEYPAD_MATRICIAL_1.col1
  N4: Part1.A3, kEYPAD_MATRICIAL_1.arrow1
  N5: Part1.A4/SDA, kEYPAD_MATRICIAL_1.col2
  N6: Part1.A5/SCL, kEYPAD_MATRICIAL_1.arrow2
  N7: Part1.ICSP_MISO, Part1.D12/MISO, Part2.MISO
  N8: Part1.D8, kEYPAD_MATRICIAL_1.arrow4
  N9: Part1.D9_PWM, Part2.RST
  N10: Part1.D10_PWM/SS, Part2.SDA
  N11: Part1.D11_PWM/MOSI, Part2.MOSI
  N12: Part1.D13/SCK, Part2.SCK
  N13: Part1.D2, L298N1.IN1
  N14: Part1.D3_PWM, L298N1.ENA, L298N1.ENB
  N15: Part1.D4, L298N1.IN2
  N16: Part1.D5_PWM, L298N1.IN3
  N17: Part1.D6_PWM, kEYPAD_MATRICIAL_1.col3
  N18: Part1.D7, kEYPAD_MATRICIAL_1.arrow3
  N19: Part1.3V3, Part2.3_3V
  5V: Part1.5V, L298N1.5V
  GND: Part1.GND, Part2.GND, M1.pin_2, M2.pin_2, M3.pin_2, L298N1.GND, Part3.GND#2, VCC1.-
  N20: L298N1.12V, VCC1.+

notes:
  power supply van de bonprinter, kon deze niet vinden in fritzing

custom parts:
  RFID-RC522-v2: A simple China made RFID-RC522 Reader; do check the pin labels, as this is a MFRC522 based clone.
  KEYPAD 4x3: KEYPAD matricial de 12 botones, 4 filas x 3 columnas
  L298N DC motor driver: 2x DC motor driver with 78M05 positive voltage regulator (7..35 V) L298N: max 46 V, 2 A Set 5 V Enable jumper to enable 5 V regultor (needed for the L298N) and +5 V output at screw terminal or supply external +5 V at screw terminal Set ENA and/or ENB to +5 V to enable motor permanently or supply ENA and/or ENB with PWM signal IN1 and IN2 set rotation directory for motor A (OUT1/OUT2) IN2 and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
